# Fritzing sketch snarky-doorbell (saved by Fritzing 0.9.3b)
breadboards: 1

parts:
  Raspberry_Pi_1 = Raspberry Pi 3 [part_number=RPI-3-V1.2]
  RE1_VOICE = Rotary Encoder [package=THT]
  R2 = Resistor [tolerance=±5% resistance=10k package=THT]
  S1_TEST = Pushbutton [package="[THT]"]
  LED2_STATUS = RGB LED (com. cathode, rgb) [package="5 mm [THT]"]
  R5 = Resistor [tolerance=±5% resistance=300 package=THT]
  R6 = Resistor [tolerance=±5% resistance=300 package=THT]
  R7 = Resistor [tolerance=±5% resistance=300 package=THT]
  RE2_STYLE = Rotary Encoder [package=THT]
  RE3_VOL = Rotary Encoder [package=THT]
  U1 = RF-LINK_RX [package=rf-link_rx]
  U2 = RF-LINK_TX [package=rf-link_tx]  # not connected

nets:
  N1: Raspberry_Pi_1.GPIO2, RE3_VOL.EncoderPinC
  N2: Raspberry_Pi_1.GPIO3, RE1_VOICE.EncoderPinC
  N3: Raspberry_Pi_1.GIPO4, RE3_VOL.EncoderPinA
  GND: Raspberry_Pi_1.GND, R2.Pin_0, LED2_STATUS.common_cathode
  N4: Raspberry_Pi_1.GIPO17, RE3_VOL.EncoderPinB
  N5: Raspberry_Pi_1.GIPO27, RE2_STYLE.EncoderPinA
  N6: Raspberry_Pi_1.GIPO22, RE1_VOICE.EncoderPinB
  N7: Raspberry_Pi_1.GIPO13, R5.Pin_1
  N8: Raspberry_Pi_1.GIPO21, U1.DATA
  N9: Raspberry_Pi_1.GIPO12, R6.Pin_1
  N10: Raspberry_Pi_1.GIPO23, RE1_VOICE.EncoderPinA
  N11: Raspberry_Pi_1.GIPO18, R7.Pin_1
  N12: Raspberry_Pi_1.GIPO15, RE2_STYLE.EncoderPinB
  N13: Raspberry_Pi_1.GIPO14, RE2_STYLE.EncoderPinC
  N14: R2.Pin_1, S1_TEST.Pin_3, S1_TEST.Pin_4
  N15: LED2_STATUS.red_anode, R5.Pin_0
  N16: LED2_STATUS.green_anode, R7.Pin_0
  N17: LED2_STATUS.blue_anode, R6.Pin_0
